// Logisim project AK2Projekt.circ as structural Verilog
module half_adder (
  input  A,
  input  B,
  output S,
  output C_out
);

  xor xor_1 (S, A, B);
  and and_1 (C_out, A, B);
endmodule

module full_adder (
  input  A,
  input  B,
  input  C_in,
  output S,
  output C_out
);

  wire half_adder_1_s, half_adder_2_c_out;

  half_adder half_adder_1 (.A(A), .B(B), .S(half_adder_1_s), .C_out(half_adder_1_s));
  half_adder half_adder_2 (.A(half_adder_1_s), .B(C_in), .S(S), .C_out(half_adder_2_c_out));
  or or_1 (C_out, half_adder_2_c_out, half_adder_1_s);
endmodule

module L_8_bit_incrementer_581b1276 (
  input  [7:0] in_1,
  output [7:0] out_2
);

  wire half_adder_1_c_out, half_adder_2_c_out, half_adder_3_c_out, half_adder_4_c_out, half_adder_5_c_out,
       half_adder_6_c_out, half_adder_7_c_out;

  half_adder half_adder_1 (.A(in_1[0]), .B(1'b1), .S(out_2[0]), .C_out(half_adder_1_c_out));
  half_adder half_adder_2 (.A(in_1[1]), .B(half_adder_1_c_out), .S(out_2[1]), .C_out(half_adder_2_c_out));
  half_adder half_adder_3 (.A(in_1[2]), .B(half_adder_2_c_out), .S(out_2[2]), .C_out(half_adder_3_c_out));
  half_adder half_adder_4 (.A(in_1[3]), .B(half_adder_3_c_out), .S(out_2[3]), .C_out(half_adder_4_c_out));
  half_adder half_adder_5 (.A(in_1[4]), .B(half_adder_4_c_out), .S(out_2[4]), .C_out(half_adder_5_c_out));
  half_adder half_adder_6 (.A(in_1[5]), .B(half_adder_5_c_out), .S(out_2[5]), .C_out(half_adder_6_c_out));
  half_adder half_adder_7 (.A(in_1[6]), .B(half_adder_6_c_out), .S(out_2[6]), .C_out(half_adder_7_c_out));
  half_adder half_adder_8 (.A(in_1[7]), .B(half_adder_7_c_out), .S(out_2[7]));  // open: C_out
endmodule

module L_8_bit_decrementer_0c0e0f55 (
  input  [7:0] data_in,
  output Bor_out,
  output [7:0] data_out
);

  wire half_subtractor_1_bor_out, half_subtractor_2_bor_out, half_subtractor_3_bor_out,
       half_subtractor_4_bor_out, half_subtractor_5_bor_out, half_subtractor_6_bor_out,
       half_subtractor_7_bor_out;

  half_subtractor half_subtractor_1 (.B(1'b1), .A(data_in[0]), .Bor_out(half_subtractor_1_bor_out), .Diff(data_out[0]));
  half_subtractor half_subtractor_2 (
    .B(half_subtractor_1_bor_out), .A(data_in[1]), .Bor_out(half_subtractor_2_bor_out), .Diff(data_out[1]));
  half_subtractor half_subtractor_3 (
    .B(half_subtractor_2_bor_out), .A(data_in[2]), .Bor_out(half_subtractor_3_bor_out), .Diff(data_out[2]));
  half_subtractor half_subtractor_4 (
    .B(half_subtractor_3_bor_out), .A(data_in[3]), .Bor_out(half_subtractor_4_bor_out), .Diff(data_out[3]));
  half_subtractor half_subtractor_5 (
    .B(half_subtractor_4_bor_out), .A(data_in[4]), .Bor_out(half_subtractor_5_bor_out), .Diff(data_out[4]));
  half_subtractor half_subtractor_6 (
    .B(half_subtractor_5_bor_out), .A(data_in[5]), .Bor_out(half_subtractor_6_bor_out), .Diff(data_out[5]));
  half_subtractor half_subtractor_7 (
    .B(half_subtractor_6_bor_out), .A(data_in[6]), .Bor_out(half_subtractor_7_bor_out), .Diff(data_out[6]));
  half_subtractor half_subtractor_8 (.B(half_subtractor_7_bor_out), .A(data_in[7]), .Bor_out(Bor_out), .Diff(Bor_out));

  assign data_out[7] = Bor_out;
endmodule

module half_subtractor (
  input  A,
  input  B,
  output Diff,
  output Bor_out
);

  wire not_1_out;

  not not_1 (not_1_out, A);
  xor xor_1 (Diff, A, B);
  and and_1 (Bor_out, not_1_out, B);
endmodule

module full_subtractor (
  input  A,
  input  B,
  input  Bor_in,
  output Diff,
  output Bor_out
);

  wire half_subtractor_1_bor_out, half_subtractor_1_diff, half_subtractor_2_bor_out;

  half_subtractor half_subtractor_1 (
    .B(Bor_in), .A(B), .Bor_out(half_subtractor_1_bor_out), .Diff(half_subtractor_1_diff));
  half_subtractor half_subtractor_2 (
    .B(half_subtractor_1_diff), .A(A), .Bor_out(half_subtractor_2_bor_out), .Diff(Diff));
  or or_1 (Bor_out, half_subtractor_2_bor_out, half_subtractor_1_bor_out);
endmodule

module mem_test_483d93b5 (
  input  [7:0] in_1,
  input  in_2,
  input  in_3,
  input  in_4,
  input  [7:0] in_5,
  input  [7:0] in_6,
  input  [7:0] in_7,
  input  in_8,
  input  in_9,
  output [7:0] out_10,
  output [7:0] out_11,
  output [7:0] out_12
);

  wire clock_1_out;

  Counter counter_1 ();  // open: clr, load, up, count, clk, D, carry, Q
  Register ACC ();  // open: D, en, clk, Q, clr
  Register B ();  // open: D, en, clk, Q, clr
  Register PSW ();  // open: D, en, clk, Q, clr
  Register register_1 (.D(in_5), .en(in_8), .Q(out_11), .clr(in_9));  // open: clk
  Register DPTR ();  // open: D, en, clk, Q, clr
  Clock clock_1 (.out(clock_1_out));
  Register SP ();  // open: D, en, clk, Q, clr
  RAM ram_1 ();  // open: addr, we, oe, clk, din, dout
  Adder adder_1 (.a(in_6), .b(in_7), .out(out_12));  // open: cin, cout
endmodule

module L_8_bit_memory_ab4ffa69 (
  input  [7:0] data_in,
  input  enable,
  input  reset,
  output [7:0] data_out
);

  Register register_1 (.D(data_in), .en(enable), .Q(data_out), .clr(reset));  // open: clk
endmodule

module L_1_bit_memory_ddd00c0c (
  input  set,
  input  enable,
  output o
);

  wire nand_1_out, nand_2_out, nand_4_out;

  nand nand_1 (nand_1_out, set, enable);
  nand nand_2 (nand_2_out, nand_1_out, enable);
  nand nand_3 (o, nand_1_out, nand_4_out);
  nand nand_4 (nand_4_out, o, nand_2_out);
endmodule

module y (
  input  [7:0] in_1,
  input  in_2,
  output [7:0] out_3
);

  L_8_bit_memory_ab4ffa69 l_8_bit_memory_ab4ffa69_1 (.enable(in_2), .data_in(in_1), .data_out(out_3));  // open: reset
endmodule

module enable (
  input  [7:0] data_in,
  input  en,
  output [7:0] data_out
);

  and and_1 (data_out[0], data_in[0], en);
  and and_2 (data_out[1], data_in[1], en);
  and and_3 (data_out[2], data_in[2], en);
  and and_4 (data_out[3], data_in[3], en);
  and and_5 (data_out[4], data_in[4], en);
  and and_6 (data_out[5], data_in[5], en);
  and and_7 (data_out[6], data_in[6], en);
  and and_8 (data_out[7], data_in[7], en);
  // AND_Gate and_9 is placed but not wired
endmodule

module ALU_AND (
  input  [7:0] A,
  input  [7:0] B,
  output [7:0] and_out
);

  and and_1 (and_out[0], A[0], B[0]);
  and and_2 (and_out[1], A[1], B[1]);
  and and_3 (and_out[2], A[2], B[2]);
  and and_4 (and_out[3], A[3], B[3]);
  and and_5 (and_out[4], A[4], B[4]);
  and and_6 (and_out[5], A[5], B[5]);
  and and_7 (and_out[6], A[6], B[6]);
  and and_8 (and_out[7], A[7], B[7]);
endmodule

module ALU_OR (
  input  [7:0] A,
  input  [7:0] B,
  output [7:0] or_out
);

  or or_1 (or_out[0], A[0], B[0]);
  or or_2 (or_out[1], A[1], B[1]);
  or or_3 (or_out[2], A[2], B[2]);
  or or_4 (or_out[3], A[3], B[3]);
  or or_5 (or_out[4], A[4], B[4]);
  or or_6 (or_out[5], A[5], B[5]);
  or or_7 (or_out[6], A[6], B[6]);
  or or_8 (or_out[7], A[7], B[7]);
endmodule

module ALU_XOR (
  input  [7:0] A,
  input  [7:0] B,
  output [7:0] xor_out
);

  xor xor_1 (xor_out[0], A[0], B[0]);
  xor xor_2 (xor_out[1], A[1], B[1]);
  xor xor_3 (xor_out[2], A[2], B[2]);
  xor xor_4 (xor_out[3], A[3], B[3]);
  xor xor_5 (xor_out[4], A[4], B[4]);
  xor xor_6 (xor_out[5], A[5], B[5]);
  xor xor_7 (xor_out[6], A[6], B[6]);
  xor xor_8 (xor_out[7], A[7], B[7]);
endmodule

module ALU_NOT (
  input  [7:0] A,
  output [7:0] not_out
);

  not not_1 (not_out[0], A[0]);
  not not_2 (not_out[1], A[1]);
  not not_3 (not_out[2], A[2]);
  not not_4 (not_out[3], A[3]);
  not not_5 (not_out[4], A[4]);
  not not_6 (not_out[5], A[5]);
  not not_7 (not_out[6], A[6]);
  not not_8 (not_out[7], A[7]);
endmodule

module ALU_CLR (
  input  [7:0] data_in,
  output [7:0] data_out
);

  and and_1 (data_out[0], data_in[0], 1'b0);
  and and_2 (data_out[1], data_in[1], 1'b0);
  and and_3 (data_out[2], data_in[2], 1'b0);
  and and_4 (data_out[3], data_in[3], 1'b0);
  and and_5 (data_out[4], data_in[4], 1'b0);
  and and_6 (data_out[5], data_in[5], 1'b0);
  and and_7 (data_out[6], data_in[6], 1'b0);
  and and_8 (data_out[7], data_in[7], 1'b0);
endmodule
