// Logisim project inc_chyba.circ as structural Verilog
module main (
  input  in_1,
  input  [7:0] in_2,
  input  in_3,
  output out_4,
  output [7:0] out_5
);

  wire and_1_out, and_2_out, and_3_out, and_4_out, and_5_out, and_6_out, and_7_out, button_1_out;
  wire [7:0] register_1_q;

  Button button_1 (.out(button_1_out));
  Register register_1 (.D(in_2), .en(in_3), .Q(register_1_q), .clk(button_1_out));  // open: clr
  xor xor_1 (out_5[0], register_1_q[0], in_1);
  and and_1 (and_1_out, in_1, register_1_q[0]);
  xor xor_2 (out_5[1], and_1_out, register_1_q[1]);
  and and_2 (and_2_out, register_1_q[1], and_1_out);
  xor xor_3 (out_5[2], and_2_out, register_1_q[2]);
  and and_3 (and_3_out, register_1_q[2], and_2_out);
  xor xor_4 (out_5[3], and_3_out, register_1_q[3]);
  and and_4 (and_4_out, register_1_q[3], and_3_out);
  xor xor_5 (out_5[4], and_4_out, register_1_q[4]);
  and and_5 (and_5_out, register_1_q[4], and_4_out);
  xor xor_6 (out_5[5], and_5_out, register_1_q[5]);
  and and_6 (and_6_out, register_1_q[5], and_5_out);
  xor xor_7 (out_5[6], and_6_out, register_1_q[6]);
  and and_7 (and_7_out, register_1_q[6], and_6_out);
  xor xor_8 (out_5[7], and_7_out, register_1_q[7]);
  and and_8 (out_4, register_1_q[7], and_7_out);
endmodule
